# Fritzing sketch udoo-experiment (saved by Fritzing 0.9.0b)
breadboards: 1

parts:
  Part1 = Arduino Due (Rev2b)
  BMP1 = BMP085 Breakout
  DHT1 = DHT11 Humitidy and Temperature Sensor
  R1 = Resistor [tolerance=±5% resistance=10k package=THT]
  GPS1 = Adafruit Ultimate GPS Breakout

nets:
  N1: Part1.D18/TX1, GPS1.RX
  N2: Part1.D19/RX1, GPS1.TX
  N3: Part1.D20/SDA3, BMP1.SDA
  N4: Part1.D21/SCL3, BMP1.SCL
  VIN: Part1.IOREF, BMP1.VIN, DHT1.VDD, R1.Pin_0, GPS1.VIN
  GND: Part1.GND, BMP1.GND, DHT1.GND, GPS1.GND
  N5: Part1.D2_PWM, DHT1.DATA, R1.Pin_1

custom parts:
  BMP085 Breakout: A breakout for the BMP085 barometric pressure and temperature sensor
  DHT11 Humitidy and Temperature Sensor: DHT11 Humidity and Temperature Sensor
